# Fritzing sketch Trailer Lighting (saved by Fritzing 0.9.1b)
circuit board: 8.46667cm x 5.64444cm
breadboards: 1

parts:
  Part1 = Arduino Uno (Rev3)
  R1 = Rotary Potentiometer (Small) [maximum_resistance=100kΩ package=THT]
  R2 = Rotary Potentiometer (Small) [maximum_resistance=10kΩ package=THT]
  R3 = Rotary Potentiometer (Small) [maximum_resistance=10kΩ package=THT]
  S1 = Toggle Switch [package=THT]
  NEOPIXEL1 = Neopixel Strip -- White (30/m)
  NEOPIXEL2 = Neopixel Strip -- White (30/m)
  C1 = Electrolytic Capacitor [capacitance=1µF package="100 mil [THT, electrolytic]"]
  R4 = Resistor [tolerance=±5% resistance=220 package=THT]
  R5 = Resistor [tolerance=±5% resistance=220 package=THT]

nets:
  N1: Part1.A0, R1.wiper
  N2: Part1.A1, R3.wiper
  N3: Part1.A2, R2.wiper
  N4: Part1.D10_PWM/SS, R5.Pin_1
  N5: Part1.D11_PWM/MOSI, R4.Pin_1
  N6: Part1.GND, R1.leg1, R2.leg1, R3.leg1, S1.COM, NEOPIXEL1.GND#3, NEOPIXEL2.GND#3, C1.-
  N7: Part1.D4, S1.L1
  N8: Part1.D5_PWM, S1.L2
  N9: Part1.5V, R1.leg2, R2.leg2, R3.leg2
  +5V: Part1.VIN, NEOPIXEL1.+5V, NEOPIXEL2.+5V, C1.+
  N10: NEOPIXEL1.DI, R4.Pin_0
  N11: NEOPIXEL2.DI, R5.Pin_0

custom parts:
  Neopixel Strip -- White (30/m): Neopixel Strip, White, 30 pixels per meter.
